// Logisim project control_logic_unit.circ as structural Verilog: 6 circuits, main circuit main
module main (
  input  in_1,
  input  in_2,
  input  in_3,
  input  in_4,
  input  in_5,
  input  in_6,
  input  in_7,
  input  in_8,
  input  in_9
);

  wire CARRY_FLAG, CLOCK0, fetch_clock, fetch_cycle, high_cycle, INT_MASK_FLAG, INT_REQUEST, inv_CLOCK,
       inv_condition_true, low_cycle, NEGATIVE_FLAG, OVERFLOW_FLAG, RESET, reset_high_cycle, reset_low_cycle,
       reset_sync, ULA_ENABLE, WRITE_ENABLE, ZERO_FLAG;
  wire [7:0] DATA, INS;
  wire [9:0] select_opcode;

  Hex_Digit_Display hex_digit_display_1 (.value(INS[7:4]));  // open: dp
  Hex_Digit_Display hex_digit_display_2 (.value(INS[3:0]));  // open: dp
  not not_1 (inv_CLOCK, CLOCK0);
  LED led_1 (.in(fetch_cycle));
  LED led_2 (.in(low_cycle));
  LED led_3 (.in(high_cycle));
  sequenciador sequenciador_1 (
    .RESET(RESET), .inv_CLOCK(inv_CLOCK), .inv_UC_restart_cycle(in_1), .inv_UC_halt(in_2),
    .reset_sync(reset_sync), .reset_low_cycle(reset_low_cycle), .reset_high_cycle(reset_high_cycle),
    .fetch_cycle(fetch_cycle), .low_cycle(low_cycle), .high_cycle(high_cycle));
  Button button_1 (.out(RESET));
  Clock clock_1 (.out(CLOCK0));
  avaliador_condicao avaliador_condicao_1 (
    .ZERO_FLAG(ZERO_FLAG), .CARRY_FLAG(CARRY_FLAG), .inv_UC_clear_cond_reg(in_6),
    .OVERFLOW_FLAG(OVERFLOW_FLAG), .inv_UC_save_cond_reg(in_7), .NEGATIVE_FLAG(NEGATIVE_FLAG),
    .inv_UC_write_enable(in_8), .inv_UC_ula_enable(in_9), .INS(INS), .inv_condition_true(inv_condition_true),
    .WRITE_ENABLE(WRITE_ENABLE), .ULA_ENABLE(ULA_ENABLE));
  decodificador decodificador_1 (
    .inv_UC_clear_interrupt_mask(in_3), .INT_REQUEST(INT_REQUEST), .inv_UC_set_interrupt_mask(in_4),
    .DATA(DATA), .reset_sync(reset_sync), .inv_UC_restart_cycle(in_1), .reset_low_cycle(reset_low_cycle),
    .reset_high_cycle(reset_high_cycle), .inv_UC_int_ready(in_5), .fetch_clock(fetch_clock),
    .fetch_cycle(fetch_cycle), .low_cycle(low_cycle), .high_cycle(high_cycle), .select_opcode(select_opcode),
    .INS(INS), .INT_MASK_FLAG(INT_MASK_FLAG));

  // Other names for the same wires on the sheet: inv_UC_clear_cond_reg = in_6; inv_UC_clear_interrupt_mask = in_3;
  //   inv_UC_halt = in_2; inv_UC_int_ready = in_5; inv_UC_restart_cycle = in_1; inv_UC_save_cond_reg = in_7;
  //   inv_UC_set_interrupt_mask = in_4; inv_UC_ula_enable = in_9; inv_UC_write_enable = in_8

  // Notes on the sheet:
  //   in_7: initial=0x1
  //   in_8: initial=0x1
  //   in_9: initial=0x1
  //   in_1: initial=0x1
  //   in_2: initial=0x1
  //   in_3: initial=0x1
  //   in_4: initial=0x1
  //   in_5: initial=0x1
  //   in_6: initial=0x1
endmodule

module sequenciador (
  input  RESET,
  input  inv_CLOCK,
  input  inv_UC_restart_cycle,
  input  inv_UC_halt,
  output reset_sync,
  output reset_low_cycle,
  output reset_high_cycle,
  output fetch_cycle,
  output low_cycle,
  output high_cycle
);

  wire inv_restart_cycle, n74138_1_pin4, n74138_1_pin10, n74138_1_pin11, n74138_1_pin12, n74138_1_pin13,
       n74138_1_pin14, n74138_1_pin15, n74193_1_pin1, n74193_1_pin4, n74193_1_pin10, n74193_1_pin11,
       n74193_1_pin15, QA, QB, QC;

  _74193 u_74193_1 (
    .pin1(n74193_1_pin1), .pin2(QB), .pin3(QA), .pin4(n74193_1_pin4), .pin5(inv_CLOCK), .pin6(QC),
    .pin15(n74193_1_pin15), .pin14(RESET), .pin11(n74193_1_pin11), .pin10(n74193_1_pin10),
    .pin9(n74193_1_pin10));  // open: pin7, pin13, pin12
  and and_1 (n74193_1_pin11, inv_restart_cycle, inv_UC_restart_cycle);
  _74138 u_74138_1 (
    .pin1(QA), .pin2(QB), .pin3(QC), .pin4(n74138_1_pin4), .pin5(n74138_1_pin4), .pin6(inv_UC_halt),
    .pin15(n74138_1_pin15), .pin14(n74138_1_pin14), .pin13(n74138_1_pin13), .pin12(n74138_1_pin12),
    .pin11(n74138_1_pin11), .pin10(n74138_1_pin10), .pin9(inv_restart_cycle));  // open: pin7
  not not_1 (reset_sync, n74138_1_pin15);
  not not_2 (reset_low_cycle, n74138_1_pin14);
  not not_3 (reset_high_cycle, n74138_1_pin13);
  not not_4 (fetch_cycle, n74138_1_pin12);
  not not_5 (low_cycle, n74138_1_pin11);
  not not_6 (high_cycle, n74138_1_pin10);
  // also tied to GND on the sheet: {n74193_1_pin10, n74138_1_pin4}
  // also tied to VCC on the sheet: {n74193_1_pin4, n74193_1_pin1, n74193_1_pin15}

  // Notes on the sheet:
  //   inv_CLOCK: initial=0x1
  //   inv_UC_restart_cycle: initial=0x1
  //   inv_UC_halt: initial=0x1
endmodule

module decodificador (
  input  inv_UC_clear_interrupt_mask,
  input  INT_REQUEST,
  input  inv_UC_set_interrupt_mask,
  input  [7:0] DATA,
  input  reset_sync,
  input  inv_UC_restart_cycle,
  input  reset_low_cycle,
  input  reset_high_cycle,
  input  inv_UC_int_ready,
  input  fetch_clock,
  input  fetch_cycle,
  input  low_cycle,
  input  high_cycle,
  output [9:0] select_opcode,
  output [7:0] INS,
  output INT_MASK_FLAG
);

  wire and_1_out, int_pending, n7474_1_pin2, n7474_1_pin4, n7474_1_pin11, n7474_1_pin12, n7474_2_pin10,
       n7474_2_pin11, n74138_1_pin7, n74138_1_pin9, n74138_1_pin10, n74138_1_pin11, n74138_1_pin12,
       n74138_1_pin13, n74138_1_pin14, n74138_1_pin15, n74157_1_pin15, n74157_2_pin15, n74377_1_pin1,
       or_1_out, Q0, Q1, Q2, Q3, Q4, Q5, Q6, Q7;

  _74377 u_74377_1 (
    .pin1(n74377_1_pin1), .pin2(Q0), .pin3(DATA[0]), .pin4(DATA[1]), .pin5(Q1), .pin6(Q2), .pin7(DATA[2]),
    .pin8(DATA[3]), .pin9(Q3), .pin19(Q7), .pin18(DATA[7]), .pin17(DATA[6]), .pin16(Q6), .pin15(Q5),
    .pin14(DATA[5]), .pin13(DATA[4]), .pin12(Q4), .pin11(fetch_clock));
  _74157 u_74157_1 (
    .pin1(fetch_cycle), .pin2(Q0), .pin3(DATA[0]), .pin4(INS[0]), .pin5(Q1), .pin6(DATA[1]), .pin7(INS[1]),
    .pin15(n74157_1_pin15), .pin14(Q3), .pin13(DATA[3]), .pin12(INS[3]), .pin11(Q2), .pin10(DATA[2]),
    .pin9(INS[2]));
  or or_1 (or_1_out, fetch_cycle, low_cycle, high_cycle);
  _74157 u_74157_2 (
    .pin1(fetch_cycle), .pin2(Q4), .pin3(DATA[4]), .pin4(INS[4]), .pin5(Q5), .pin6(DATA[5]), .pin7(INS[5]),
    .pin15(n74157_2_pin15), .pin14(Q7), .pin13(DATA[7]), .pin12(INS[7]), .pin11(Q6), .pin10(DATA[6]),
    .pin9(INS[6]));
  _74138 u_74138_1 (
    .pin1(INS[5]), .pin2(INS[6]), .pin3(INS[7]), .pin4(select_opcode[8]), .pin5(select_opcode[8]),
    .pin6(or_1_out), .pin7(n74138_1_pin7), .pin15(n74138_1_pin15), .pin14(n74138_1_pin14),
    .pin13(n74138_1_pin13), .pin12(n74138_1_pin12), .pin11(n74138_1_pin11), .pin10(n74138_1_pin10),
    .pin9(n74138_1_pin9));
  not not_1 (select_opcode[0], n74138_1_pin15);
  not not_2 (select_opcode[1], n74138_1_pin14);
  not not_3 (select_opcode[2], n74138_1_pin13);
  not not_4 (select_opcode[3], n74138_1_pin12);
  not not_5 (select_opcode[4], n74138_1_pin11);
  not not_6 (select_opcode[5], n74138_1_pin10);
  not not_7 (select_opcode[6], n74138_1_pin9);
  not not_8 (select_opcode[7], n74138_1_pin7);
  or or_2 (select_opcode[9], reset_sync, reset_low_cycle, reset_high_cycle);
  and and_1 (and_1_out, INT_REQUEST, INT_MASK_FLAG);
  _7474 u_7474_1 (
    .pin1(inv_UC_int_ready), .pin2(n7474_1_pin2), .pin3(and_1_out), .pin4(n7474_1_pin4), .pin5(int_pending),
    .pin13(inv_UC_clear_interrupt_mask), .pin12(n7474_1_pin12), .pin11(n7474_1_pin11),
    .pin10(inv_UC_set_interrupt_mask), .pin9(INT_MASK_FLAG));  // open: pin6, pin8
  _7474 u_7474_2 (
    .pin13(inv_UC_restart_cycle), .pin12(int_pending), .pin11(n7474_2_pin11), .pin10(n7474_2_pin10),
    .pin9(select_opcode[8]));  // open: pin1, pin2, pin3, pin4, pin5, pin6, pin8
  not not_9 (n7474_2_pin11, inv_UC_int_ready);
  // also tied to GND on the sheet: {n74377_1_pin1, n74157_1_pin15, n74157_2_pin15, n7474_1_pin12, n7474_1_pin11}
  // also tied to VCC on the sheet: {n7474_1_pin2, n7474_1_pin4, n7474_2_pin10}

  // Other names for the same wires on the sheet: select_opcode_int = select_opcode[8]

  // Notes on the sheet:
  //   inv_UC_restart_cycle: initial=0x1
  //   inv_UC_set_interrupt_mask: initial=0x1
  //   inv_UC_clear_interrupt_mask: initial=0x1
endmodule

module avaliador_condicao (
  input  ZERO_FLAG,
  input  CARRY_FLAG,
  input  inv_UC_clear_cond_reg,
  input  OVERFLOW_FLAG,
  input  inv_UC_save_cond_reg,
  input  NEGATIVE_FLAG,
  input  inv_UC_write_enable,
  input  inv_UC_ula_enable,
  input  [7:0] INS,
  output inv_condition_true,
  output WRITE_ENABLE,
  output ULA_ENABLE
);

  wire and_1_out, n7474_1_pin4, not_1_out, or_1_out, or_2_out, or_3_out, or_4_out, xor_1_out, xor_2_out,
       xor_3_out, xor_4_out;

  xor xor_1 (xor_1_out, ZERO_FLAG, INS[4]);
  xor xor_2 (xor_2_out, CARRY_FLAG, INS[4]);
  xor xor_3 (xor_3_out, OVERFLOW_FLAG, INS[4]);
  xor xor_4 (xor_4_out, NEGATIVE_FLAG, INS[4]);
  or or_1 (or_1_out, xor_1_out, INS[0]);
  or or_2 (or_2_out, xor_2_out, INS[1]);
  or or_3 (or_3_out, xor_3_out, INS[2]);
  or or_4 (or_4_out, xor_4_out, INS[3]);
  and and_1 (and_1_out, or_1_out, or_2_out, or_3_out, or_4_out);
  not not_1 (not_1_out, inv_UC_save_cond_reg);
  _7474 u_7474_1 (
    .pin1(inv_UC_clear_cond_reg), .pin2(and_1_out), .pin3(not_1_out), .pin4(n7474_1_pin4),
    .pin5(inv_condition_true));  // open: pin6, pin13, pin12, pin11, pin10, pin9, pin8
  nor nor_1 (WRITE_ENABLE, inv_condition_true, inv_UC_write_enable);
  nor nor_2 (ULA_ENABLE, inv_condition_true, inv_UC_ula_enable);
  // also tied to VCC on the sheet: n7474_1_pin4
endmodule

module ucode_template (
  input  fetch_cycle,
  input  low_cycle,
  input  high_cycle,
  input  select_opcode,
  output inv_UC_read_addr_src_reg,
  output inv_UC_int_ready,
  output inv_UC_B,
  output inv_UC_write_address,
  output inv_UC_restart_cycle,
  output inv_UC_ula_enable,
  output inv_UC_A,
  output inv_UC_pcia_swap,
  output inv_UC_save_src_reg,
  output inv_UC_extended_opcode,
  output inv_UC_write_enable,
  output inv_UC_save_cond_reg,
  output inv_UC_clear_cond_reg,
  output inv_UC_read_mem_const
);

  wire and_1_out, and_2_out, and_3_out;

  assign inv_UC_write_enable = and_1_out ? 1'b0 : 1'bz;  // Controlled_Buffer controlled_buffer_1
  and and_1 (and_1_out, fetch_cycle, select_opcode);
  assign inv_UC_write_enable = and_2_out ? 1'b0 : 1'bz;  // Controlled_Buffer controlled_buffer_2
  and and_2 (and_2_out, low_cycle, select_opcode);
  assign inv_UC_write_enable = and_3_out ? 1'b0 : 1'bz;  // Controlled_Buffer controlled_buffer_3
  and and_3 (and_3_out, high_cycle, select_opcode);
  assign inv_UC_write_address = and_1_out ? 1'b0 : 1'bz;  // Controlled_Buffer controlled_buffer_4
  assign inv_UC_write_address = and_2_out ? 1'b0 : 1'bz;  // Controlled_Buffer controlled_buffer_5
  assign inv_UC_write_address = and_3_out ? 1'b0 : 1'bz;  // Controlled_Buffer controlled_buffer_6
  assign inv_UC_pcia_swap = and_1_out ? 1'b0 : 1'bz;  // Controlled_Buffer controlled_buffer_7
  assign inv_UC_pcia_swap = and_2_out ? 1'b0 : 1'bz;  // Controlled_Buffer controlled_buffer_8
  assign inv_UC_pcia_swap = and_3_out ? 1'b0 : 1'bz;  // Controlled_Buffer controlled_buffer_9
  assign inv_UC_read_addr_src_reg = and_1_out ? 1'b0 : 1'bz;  // Controlled_Buffer controlled_buffer_10
  assign inv_UC_read_addr_src_reg = and_2_out ? 1'b0 : 1'bz;  // Controlled_Buffer controlled_buffer_11
  assign inv_UC_read_addr_src_reg = and_3_out ? 1'b0 : 1'bz;  // Controlled_Buffer controlled_buffer_12
  assign inv_UC_save_cond_reg = and_1_out ? 1'b0 : 1'bz;  // Controlled_Buffer controlled_buffer_13
  assign inv_UC_save_cond_reg = and_2_out ? 1'b0 : 1'bz;  // Controlled_Buffer controlled_buffer_14
  assign inv_UC_save_cond_reg = and_3_out ? 1'b0 : 1'bz;  // Controlled_Buffer controlled_buffer_15
  assign inv_UC_restart_cycle = and_1_out ? 1'b0 : 1'bz;  // Controlled_Buffer controlled_buffer_16
  assign inv_UC_restart_cycle = and_2_out ? 1'b0 : 1'bz;  // Controlled_Buffer controlled_buffer_17
  assign inv_UC_restart_cycle = and_3_out ? 1'b0 : 1'bz;  // Controlled_Buffer controlled_buffer_18
  assign inv_UC_save_src_reg = and_1_out ? 1'b0 : 1'bz;  // Controlled_Buffer controlled_buffer_19
  assign inv_UC_int_ready = and_1_out ? 1'b0 : 1'bz;  // Controlled_Buffer controlled_buffer_20
  assign inv_UC_save_src_reg = and_2_out ? 1'b0 : 1'bz;  // Controlled_Buffer controlled_buffer_21
  assign inv_UC_int_ready = and_2_out ? 1'b0 : 1'bz;  // Controlled_Buffer controlled_buffer_22
  assign inv_UC_save_src_reg = and_3_out ? 1'b0 : 1'bz;  // Controlled_Buffer controlled_buffer_23
  assign inv_UC_int_ready = and_3_out ? 1'b0 : 1'bz;  // Controlled_Buffer controlled_buffer_24
  assign inv_UC_clear_cond_reg = and_1_out ? 1'b0 : 1'bz;  // Controlled_Buffer controlled_buffer_25
  assign inv_UC_clear_cond_reg = and_2_out ? 1'b0 : 1'bz;  // Controlled_Buffer controlled_buffer_26
  assign inv_UC_clear_cond_reg = and_3_out ? 1'b0 : 1'bz;  // Controlled_Buffer controlled_buffer_27
  assign inv_UC_ula_enable = and_1_out ? 1'b0 : 1'bz;  // Controlled_Buffer controlled_buffer_28
  assign inv_UC_ula_enable = and_2_out ? 1'b0 : 1'bz;  // Controlled_Buffer controlled_buffer_29
  assign inv_UC_ula_enable = and_3_out ? 1'b0 : 1'bz;  // Controlled_Buffer controlled_buffer_30
  assign inv_UC_extended_opcode = and_1_out ? 1'b0 : 1'bz;  // Controlled_Buffer controlled_buffer_31
  assign inv_UC_extended_opcode = and_2_out ? 1'b0 : 1'bz;  // Controlled_Buffer controlled_buffer_32
  assign inv_UC_extended_opcode = and_3_out ? 1'b0 : 1'bz;  // Controlled_Buffer controlled_buffer_33
  assign inv_UC_B = and_1_out ? 1'b0 : 1'bz;  // Controlled_Buffer controlled_buffer_34
  assign inv_UC_B = and_2_out ? 1'b0 : 1'bz;  // Controlled_Buffer controlled_buffer_35
  assign inv_UC_B = and_3_out ? 1'b0 : 1'bz;  // Controlled_Buffer controlled_buffer_36
  assign inv_UC_read_mem_const = and_1_out ? 1'b0 : 1'bz;  // Controlled_Buffer controlled_buffer_37
  assign inv_UC_read_mem_const = and_2_out ? 1'b0 : 1'bz;  // Controlled_Buffer controlled_buffer_38
  assign inv_UC_read_mem_const = and_3_out ? 1'b0 : 1'bz;  // Controlled_Buffer controlled_buffer_39
  assign inv_UC_A = and_1_out ? 1'b0 : 1'bz;  // Controlled_Buffer controlled_buffer_40
  assign inv_UC_A = and_2_out ? 1'b0 : 1'bz;  // Controlled_Buffer controlled_buffer_41
  assign inv_UC_A = and_3_out ? 1'b0 : 1'bz;  // Controlled_Buffer controlled_buffer_42
endmodule

module ucode_0 (
  input  fetch_cycle,
  input  low_cycle,
  input  high_cycle,
  input  select_opcode,
  output inv_UC_read_addr_src_reg,
  output inv_UC_int_ready,
  output inv_UC_B,
  output inv_UC_write_address,
  output inv_UC_restart_cycle,
  output inv_UC_ula_enable,
  output inv_UC_A,
  output inv_UC_pcia_swap,
  output inv_UC_save_src_reg,
  output inv_UC_extended_opcode,
  output inv_UC_write_enable,
  output inv_UC_save_cond_reg,
  output inv_UC_clear_cond_reg,
  output inv_UC_read_mem_const
);

  wire and_1_out, and_2_out, and_3_out;

  and and_1 (and_1_out, fetch_cycle, select_opcode);
  and and_2 (and_2_out, low_cycle, select_opcode);
  and and_3 (and_3_out, high_cycle, select_opcode);
  assign inv_UC_restart_cycle = and_2_out ? 1'b0 : 1'bz;  // Controlled_Buffer controlled_buffer_1
  assign inv_UC_extended_opcode = and_1_out ? 1'b0 : 1'bz;  // Controlled_Buffer controlled_buffer_2
endmodule
